// Logisim project Four_Bits_Add_Sub.circ as structural Verilog: 2 circuits, main circuit Add_Sub_4Bits
module Add_Sub_4Bits (
  input  [3:0] A,
  input  [3:0] B,
  input  Add_Sub,
  output [3:0] R,
  output Zero,
  output Overflow
);

  wire add_1bit_1_cout, add_1bit_2_cout, add_1bit_3_cout, add_1bit_4_cout, and_1_out, and_3_out, not_1_out,
       not_2_out, not_3_out, not_4_out, not_5_out, xnor_1_out, xnor_2_out, xnor_3_out, xnor_4_out;

  // Probe on A
  xnor xnor_1 (xnor_1_out, B[3], Add_Sub);
  // Probe on B
  xnor xnor_2 (xnor_2_out, B[1], Add_Sub);
  xnor xnor_3 (xnor_3_out, B[2], Add_Sub);
  xnor xnor_4 (xnor_4_out, B[0], Add_Sub);
  Add_1Bit add_1bit_1 (.Cout(add_1bit_1_cout), .Sum(R[0]), .B(A[0]), .A(xnor_4_out), .Cin(not_1_out));
  Add_1Bit add_1bit_2 (.Cout(add_1bit_2_cout), .Sum(R[1]), .B(A[1]), .A(xnor_2_out), .Cin(add_1bit_1_cout));
  Add_1Bit add_1bit_3 (.Cout(add_1bit_3_cout), .Sum(R[2]), .B(A[2]), .A(xnor_3_out), .Cin(add_1bit_2_cout));
  Add_1Bit add_1bit_4 (.Cout(add_1bit_4_cout), .Sum(R[3]), .B(A[3]), .A(xnor_1_out), .Cin(add_1bit_3_cout));
  not not_1 (not_1_out, Add_Sub);
  // Probe on R
  and and_1 (and_1_out, not_2_out, not_5_out);
  not not_2 (not_2_out, R[0]);
  and and_2 (Zero, and_1_out, and_3_out);
  and and_3 (and_3_out, not_3_out, not_4_out);
  not not_3 (not_3_out, R[2]);
  not not_4 (not_4_out, R[3]);
  not not_5 (not_5_out, R[1]);
  xor xor_1 (Overflow, add_1bit_3_cout, add_1bit_4_cout);

  // Notes on the sheet:
  //   Simon Zheng 260744353
  //   MAKE SURE THAT YOU OPENED THIS PROJECT IN "LOGISIM-EVOLUTION"
  //   YOU CAN FIND "LOGISIM-EVOLUTION" PROGRAM IN THE ASSIGNMENT'S FOLDER
  //   DO NOT USE "LOGISIM" VERSION TO SOLVE THIS ASSIGNMENT!
endmodule

module Add_1Bit (
  input  Cin,
  input  A,
  input  B,
  output Sum,
  output Cout
);

  wire and_1_out, and_2_out, xor_1_out;

  xor xor_1 (xor_1_out, A, B);
  and and_1 (and_1_out, xor_1_out, Cin);
  and and_2 (and_2_out, A, B);
  xor xor_2 (Sum, Cin, xor_1_out);
  or or_1 (Cout, and_1_out, and_2_out);

  // Notes on the sheet:
  //   Simon Zheng 260744353
  //   MAKE SURE THAT YOU OPENED THIS PROJECT IN "LOGISIM-EVOLUTION"
  //   YOU CAN FIND "LOGISIM-EVOLUTION" PROGRAM IN THE ASSIGNMENT'S FOLDER
  //   DO NOT USE "LOGISIM" VERSION TO SOLVE THIS ASSIGNMENT!
endmodule
